// Logisim project CODE.circ as structural Verilog
module XOR (
  input  A_In,
  input  B_In,
  output Out
);

  wire nand_1_out, or_1_out;

  or or_1 (or_1_out, A_In, B_In);
  nand nand_1 (nand_1_out, A_In, B_In);
  and and_1 (Out, or_1_out, nand_1_out);
endmodule

module Half_Adder (
  input  A_In,
  input  B_In,
  output Sum_Out,
  output Carry_Out
);

  XOR xor_1 (.A_In(A_In), .B_In(B_In), .Out(Sum_Out));
  and and_1 (Carry_Out, A_In, B_In);
endmodule

module Full_Adder (
  input  Carry_In,
  input  A_In,
  input  B_In,
  output Sum_Out,
  output Carry_Out
);

  wire half_adder_1_carry_out, half_adder_1_sum_out, half_adder_2_carry_out;

  Half_Adder half_adder_1 (
    .A_In(A_In), .B_In(B_In), .Sum_Out(half_adder_1_sum_out), .Carry_Out(half_adder_1_carry_out));
  Half_Adder half_adder_2 (
    .A_In(Carry_In), .B_In(half_adder_1_sum_out), .Sum_Out(Sum_Out), .Carry_Out(half_adder_2_carry_out));
  or or_1 (Carry_Out, half_adder_2_carry_out, half_adder_1_carry_out);
endmodule

module _8_Bit_Adder (
  input  Carry_In,
  input  [7:0] BIn8_0to7,
  input  [7:0] AIn_0to7,
  output [7:0] SumOut8_0to7,
  output Carry_Out
);

  wire full_adder_1_carry_out, full_adder_2_carry_out, full_adder_3_carry_out, full_adder_4_carry_out,
       full_adder_5_carry_out, full_adder_6_carry_out, full_adder_7_carry_out;

  Full_Adder full_adder_1 (
    .A_In(AIn_0to7[0]), .B_In(BIn8_0to7[0]), .Carry_In(Carry_In), .Carry_Out(full_adder_1_carry_out),
    .Sum_Out(SumOut8_0to7[0]));
  Full_Adder full_adder_2 (
    .A_In(AIn_0to7[1]), .B_In(BIn8_0to7[1]), .Carry_In(full_adder_1_carry_out),
    .Carry_Out(full_adder_2_carry_out), .Sum_Out(SumOut8_0to7[1]));
  Full_Adder full_adder_3 (
    .A_In(AIn_0to7[2]), .B_In(BIn8_0to7[2]), .Carry_In(full_adder_2_carry_out),
    .Carry_Out(full_adder_3_carry_out), .Sum_Out(SumOut8_0to7[2]));
  Full_Adder full_adder_4 (
    .A_In(AIn_0to7[3]), .B_In(BIn8_0to7[3]), .Carry_In(full_adder_3_carry_out),
    .Carry_Out(full_adder_4_carry_out), .Sum_Out(SumOut8_0to7[3]));
  Full_Adder full_adder_5 (
    .A_In(AIn_0to7[4]), .B_In(BIn8_0to7[4]), .Carry_In(full_adder_4_carry_out),
    .Carry_Out(full_adder_5_carry_out), .Sum_Out(SumOut8_0to7[4]));
  Full_Adder full_adder_6 (
    .A_In(AIn_0to7[5]), .B_In(BIn8_0to7[5]), .Carry_In(full_adder_5_carry_out),
    .Carry_Out(full_adder_6_carry_out), .Sum_Out(SumOut8_0to7[5]));
  Full_Adder full_adder_7 (
    .A_In(AIn_0to7[6]), .B_In(BIn8_0to7[6]), .Carry_In(full_adder_6_carry_out),
    .Carry_Out(full_adder_7_carry_out), .Sum_Out(SumOut8_0to7[6]));
  Full_Adder full_adder_8 (
    .A_In(AIn_0to7[7]), .B_In(BIn8_0to7[7]), .Carry_In(full_adder_7_carry_out), .Carry_Out(Carry_Out),
    .Sum_Out(SumOut8_0to7[7]));
endmodule

module One_s_Compliment (
  input  Invert,
  input  [7:0] Input8_0to7,
  output [7:0] Output8_0to7
);

  XOR xor_1 (.A_In(Input8_0to7[0]), .B_In(Invert), .Out(Output8_0to7[0]));
  XOR xor_2 (.A_In(Input8_0to7[1]), .B_In(Invert), .Out(Output8_0to7[1]));
  XOR xor_3 (.A_In(Input8_0to7[2]), .B_In(Invert), .Out(Output8_0to7[2]));
  XOR xor_4 (.A_In(Input8_0to7[3]), .B_In(Invert), .Out(Output8_0to7[3]));
  XOR xor_5 (.A_In(Input8_0to7[4]), .B_In(Invert), .Out(Output8_0to7[4]));
  XOR xor_6 (.A_In(Input8_0to7[5]), .B_In(Invert), .Out(Output8_0to7[5]));
  XOR xor_7 (.A_In(Input8_0to7[6]), .B_In(Invert), .Out(Output8_0to7[6]));
  XOR xor_8 (.A_In(Input8_0to7[7]), .B_In(Invert), .Out(Output8_0to7[7]));
endmodule

module _8_Bit_Adder_Subtractor (
  input  Sub,
  input  [7:0] Subtrahand8_0to7,
  input  [7:0] Minuend8_0to7,
  output [7:0] SumOut8_0to7,
  output Overflow_Underflow
);

  wire n8_bit_adder_1_carry_out;
  wire [7:0] one_s_compliment_1_output8_0to7;

  One_s_Compliment one_s_compliment_1 (
    .Input8_0to7(Subtrahand8_0to7), .Invert(Sub), .Output8_0to7(one_s_compliment_1_output8_0to7));
  _8_Bit_Adder u_8_bit_adder_1 (
    .BIn8_0to7(one_s_compliment_1_output8_0to7), .AIn_0to7(Minuend8_0to7), .Carry_In(Sub),
    .Carry_Out(n8_bit_adder_1_carry_out), .SumOut8_0to7(SumOut8_0to7));
  XOR xor_1 (.A_In(Sub), .B_In(n8_bit_adder_1_carry_out), .Out(Overflow_Underflow));
endmodule
